// Logisim project Milestone2.circ as structural Verilog: 3 circuits, main circuit main
module main (
  output E
);

  wire CLK, I, INC_DR, INC_PC, LD_AC, LD_AR, LD_DR, LD_IR, LD_PC, READ_MEM, WR_MEM;
  wire [2:0] ALU_SLCT, BUS_SLCT;
  wire [6:0] AR, bit_extender_1_out, bit_extender_2_out, PC_q;
  wire [15:0] AC, alu_1_z, bit_extender_3_out, bit_extender_4_out, DR, IR, multiplexer_1_out, ram_1_data,
       TR_q;

  Bit_Extender #(.in_width(16), .out_width(7)) bit_extender_1 (.in(multiplexer_1_out), .out(bit_extender_1_out));
  Bit_Extender #(.in_width(16), .out_width(7)) bit_extender_2 (.in(multiplexer_1_out), .out(bit_extender_2_out));
  Clock clock_1 (.out(CLK));
  RAM #(.addrWidth(7), .dataWidth(16), .bus("separate")) ram_1 (
    .addr(AR), .din(multiplexer_1_out), .data(ram_1_data), .str(WR_MEM), .clk(CLK), .ld(READ_MEM));  // open: sel, clr
  Register #(.width(7)) u_AR (.D(bit_extender_1_out), .en(LD_AR), .Q(AR), .clk(CLK));  // open: clr
  Counter #(.width(7), .max('h7f)) PC (
    .load(LD_PC), .D(bit_extender_2_out), .count(INC_PC), .Q(PC_q), .clk(CLK));  // open: carry, clr
  Register #(.width(16)) u_AC (.D(alu_1_z), .en(LD_AC), .Q(AC), .clk(CLK));  // open: clr
  Counter #(.width(16), .max('hffff)) u_DR (
    .load(LD_DR), .D(multiplexer_1_out), .count(INC_DR), .Q(DR), .clk(CLK));  // open: carry, clr
  Register #(.width(16)) TR (.D(multiplexer_1_out), .en(1'b0), .Q(TR_q), .clk(CLK));  // open: clr
  Register #(.width(16)) u_IR (.D(multiplexer_1_out), .en(LD_IR), .Q(IR), .clk(CLK));  // open: clr
  CU cu_1 (
    .IR(IR), .CLK(CLK), .AC(AC), .RD_MEM(READ_MEM), .I(I), .BUS_SLCT(BUS_SLCT), .ALU_SLCT(ALU_SLCT),
    .WR_MEM(WR_MEM), .LD_AR(LD_AR), .LD_PC(LD_PC), .LD_DR(LD_DR), .INC_DR(INC_DR), .LD_IR(LD_IR),
    .LD_AC(LD_AC), .DR(DR), .INC_PC(INC_PC));
  assign bit_extender_3_out = {{9{1'b0}}, AR};  // Bit_Extender bit_extender_3
  assign bit_extender_4_out = {{9{1'b0}}, PC_q};  // Bit_Extender bit_extender_4
  ALU alu_1 (.B(AC), .Z(alu_1_z), .Controls(ALU_SLCT), .Overflow(E), .A(DR));
  Multiplexer #(.select(3), .width(16)) multiplexer_1 (
    .in0(ram_1_data), .in1(bit_extender_3_out), .in2(bit_extender_4_out), .in3(AC), .in4(DR), .in5(TR_q),
    .in7(IR), .out(multiplexer_1_out), .sel(BUS_SLCT));  // open: in6, en

  // Notes on the sheet:
  //   Basic Computer
endmodule

module ALU (
  input  [15:0] A,
  input  [15:0] B,
  input  [2:0] Controls,
  output Overflow,
  output [15:0] Z
);

  wire adder_1_cout, adder_2_cout, bitselector_1_out, subtractor_1_bout;
  wire [15:0] adder_1_out, adder_2_out, divider_1_out, multiplier_1_cout, multiplier_1_out, subtractor_1_out,
       xor_1_out;

  BitSelector #(.width(16)) bitselector_1 (.in(multiplier_1_cout), .out(bitselector_1_out), .sel(4'b0000));
  Adder #(.width(16)) adder_1 (.a(A), .b({16{1'b0}}), .out(adder_1_out), .cin(1'b1), .cout(adder_1_cout));
  Multiplier #(.width(16)) multiplier_1 (.a(A), .b(B), .out(multiplier_1_out), .cout(multiplier_1_cout));  // open: cin
  Subtractor #(.width(16)) subtractor_1 (.a(A), .b(B), .out(subtractor_1_out), .bin(1'b0), .bout(subtractor_1_bout));
  Divider #(.width(16)) divider_1 (.a(A), .b(B), .out(divider_1_out));  // open: upper, rem
  Adder #(.width(16)) adder_2 (.a(A), .b(B), .out(adder_2_out), .cin(1'b0), .cout(adder_2_cout));
  assign xor_1_out = A ^ B;  // XOR_Gate xor_1, 16 bits wide
  or or_1 (Overflow, adder_2_cout, subtractor_1_bout, bitselector_1_out, adder_1_cout);
  Multiplexer #(.select(3), .width(16), .enable("false")) multiplexer_1 (
    .in0({16{1'b0}}), .in1(A), .in2(adder_1_out), .in3(multiplier_1_out), .in4(subtractor_1_out),
    .in5(divider_1_out), .in6(adder_2_out), .in7(xor_1_out), .out(Z), .sel(Controls));
endmodule

module CU (
  input  [15:0] IR,
  input  CLK,
  input  [15:0] AC,
  input  [15:0] DR,
  output RD_MEM,
  output I,
  output [2:0] BUS_SLCT,
  output [2:0] ALU_SLCT,
  output LD_AC,
  output WR_MEM,
  output LD_DR,
  output LD_AR,
  output LD_PC,
  output INC_DR,
  output LD_IR,
  output INC_PC
);

  wire and_5_out, CLR_SC, D0, D0_T4, D0_T5, D0_T6, D1, D1_T4, D1_T5, D2, D2_T4, D2_T5, D3, D3_T4, D4, D5,
       D5_T4, D5_T5, D6, D6_T4, D6_T6, D7, d_ff_1_q, or_1_out, or_2_out, or_3_out, T0, T2, T3, T4, T5, T6,
       T7, T8, Zero_AC, Zero_DR;
  wire [3:0] SC_q;

  D_Flip_Flop d_ff_1 (.clk(CLK), .D(CLR_SC), .Q(d_ff_1_q));  // open: Qn, preset, en, reset
  D_Flip_Flop d_ff_2 (.clk(CLK), .D(IR[15]), .Q(I));  // open: Qn, preset, en, reset
  Counter #(.width(4), .max('hf)) SC (.Q(SC_q), .clk(CLK), .clr(d_ff_1_q));  // open: load, D, count, carry
  Decoder #(.select(4)) decoder_1 (
    .out0(T0), .out1(LD_IR), .out2(T2), .out3(T3), .out4(T4), .out5(T5), .out6(T6), .out7(T7), .out8(T8),
    .sel(SC_q));  // open: out9, out10, out11, out12, out13, out14, out15, en
  Decoder #(.select(3)) decoder_2 (
    .out0(D0), .out1(D1), .out2(D2), .out3(D3), .out4(D4), .out5(D5), .out6(D6), .out7(D7), .sel(IR[14:12]));  // open: en
  nor nor_1 (Zero_AC, AC[0], AC[1], AC[2], AC[3], AC[4], AC[5], AC[6], AC[7], AC[8], AC[9], AC[10], AC[11], AC[12], AC[13], AC[14], AC[15]);
  nor nor_2 (Zero_DR, DR[0], DR[1], DR[2], DR[3], DR[4], DR[5], DR[6], DR[7], DR[8], DR[9], DR[10], DR[11], DR[12], DR[13], DR[14], DR[15]);
  or or_1 (or_1_out, D6_T6, D0_T5, D2_T5);
  or CLR (CLR_SC, D0_T6, D1_T5, D2_T5, D3_T4, LD_PC, D5_T5, D6_T6);
  or or_2 (or_2_out, D3_T4, D0_T5);
  or or_3 (or_3_out, D0_T5, D2_T5);
  and and_1 (D0_T4, D0, T4);
  and and_2 (D1_T4, D1, T4);
  and and_3 (D2_T4, D2, T4);
  and and_4 (D3_T4, D3, T4);
  and and_5 (and_5_out, Zero_DR, D6_T6);
  or u_RD_MEM (RD_MEM, D0_T4, D1_T4, D2_T4, D5_T4, D6_T4, LD_IR);
  Priority_Encoder priority_encoder_1 (
    .in0(RD_MEM), .in1(LD_PC), .in2(T0), .in3(or_2_out), .in4(or_1_out), .in7(T2), .out(BUS_SLCT));  // open: in5, in6, en_in, gs, en_out
  or or_4 (WR_MEM, D3_T4, D6_T6);
  or or_5 (LD_AR, T0, T2);
  or or_6 (INC_PC, and_5_out, LD_IR);
  Priority_Encoder priority_encoder_2 (
    .in1(or_3_out), .in2(INC_DR), .in3(D5_T5), .in5(D0_T6), .in6(D1_T5), .out(ALU_SLCT));  // open: in0, in4, in7, en_in, gs, en_out
  and and_6 (LD_PC, D4, T4);
  and and_7 (D5_T4, D5, T4);
  and and_8 (D6_T4, D6, T4);
  or or_7 (LD_DR, D0_T4, D1_T4, D2_T4, D5_T4, D6_T4, D0_T5);
  and and_9 (D6_T6, D6, T6);
  and and_10 (D0_T5, D0, T5);
  and and_11 (D1_T5, D1, T5);
  and and_12 (D2_T5, D2, T5);
  and and_13 (D0_T6, D0, T6);
  or or_8 (LD_AC, D0_T5, D1_T5, D0_T6, D2_T5, D5_T5);
  and and_14 (D5_T5, D5, T5);
  and and_15 (INC_DR, D6, T5);

  // Other names for the same wires on the sheet: D4_T4 = LD_PC; D6_T5 = INC_DR; T1 = LD_IR
endmodule
